// Logisim project GuessTheNumber.circ as structural Verilog: 17 circuits, main circuit main
module main (
  input  JOGAR,
  input  JOGADOR,
  input  A3,
  input  A2,
  input  A1,
  input  A0,
  input  B3,
  input  B2,
  input  B1,
  input  B0,
  output MAIOR,
  output ACERTOU,
  output MENOR
);

  wire decode_1_d_a, decode_1_d_b, decode_1_d_c, decode_1_d_d, decode_1_d_e, decode_1_d_f, decode_1_d_g,
       decode_2_d_a, decode_2_d_b, decode_2_d_c, decode_2_d_d, decode_2_d_e, decode_2_d_f, decode_2_d_g;

  _7_Segment_Display u_7_segment_display_1 (
    .g(decode_1_d_g), .f(decode_1_d_f), .a(decode_1_d_a), .b(decode_1_d_b), .e(decode_1_d_e),
    .d(decode_1_d_d), .c(decode_1_d_c));  // open: dp
  _7_Segment_Display u_7_segment_display_2 (
    .g(decode_2_d_g), .f(decode_2_d_f), .a(decode_2_d_a), .b(decode_2_d_b), .e(decode_2_d_e),
    .d(decode_2_d_d), .c(decode_2_d_c));  // open: dp
  decode decode_1 (
    .B3(A3), .B2(A2), .B1(A1), .B0(A0), .D_A(decode_1_d_a), .D_B(decode_1_d_b), .D_C(decode_1_d_c),
    .D_D(decode_1_d_d), .D_E(decode_1_d_e), .D_F(decode_1_d_f), .D_G(decode_1_d_g));
  decode decode_2 (
    .B3(B3), .B2(B2), .B1(B1), .B0(B0), .D_A(decode_2_d_a), .D_B(decode_2_d_b), .D_C(decode_2_d_c),
    .D_D(decode_2_d_d), .D_E(decode_2_d_e), .D_F(decode_2_d_f), .D_G(decode_2_d_g));
  game game_1 (
    .Jogar(JOGAR), .Jogador(JOGADOR), .A3(A3), .A2(A2), .A1(A1), .A0(A0), .B3(B3), .B2(B2), .B1(B1), .B0(B0),
    .Maior(MAIOR), .Igual(ACERTOU), .Menor(MENOR));
endmodule

module game (
  input  Jogar,
  input  Jogador,
  input  A3,
  input  A2,
  input  A1,
  input  A0,
  input  B3,
  input  B2,
  input  B1,
  input  B0,
  output Maior,
  output Igual,
  output Menor
);

  wire comparador_1_igual, comparador_1_maior, comparador_1_menor, mux2x1_4_bits_1_c0, mux2x1_4_bits_1_c1,
       mux2x1_4_bits_1_c2, mux2x1_4_bits_1_c3;

  mux2x1_4_bits mux2x1_4_bits_1 (
    .S(Jogador), .A0(A0), .B0(B0), .A1(A1), .B1(B1), .A2(A2), .B2(B2), .A3(A3), .B3(B3),
    .C0(mux2x1_4_bits_1_c0), .C1(mux2x1_4_bits_1_c1), .C2(mux2x1_4_bits_1_c2), .C3(mux2x1_4_bits_1_c3));
  comparador comparador_1 (
    .A0(mux2x1_4_bits_1_c0), .A1(mux2x1_4_bits_1_c1), .A2(mux2x1_4_bits_1_c2), .A3(mux2x1_4_bits_1_c3),
    .B0(1'b0), .B1(1'b1), .B2(1'b1), .B3(1'b1), .Maior(comparador_1_maior), .Igual(comparador_1_igual),
    .Menor(comparador_1_menor));
  and and_1 (Maior, Jogar, comparador_1_maior);
  and and_2 (Igual, Jogar, comparador_1_igual);
  and and_3 (Menor, Jogar, comparador_1_menor);
endmodule

module mux (
  input  A,
  input  B,
  input  S,
  output C
);

  wire and_1_out, and_2_out, not_1_out;

  not not_1 (not_1_out, S);
  and and_1 (and_1_out, not_1_out, A);
  and and_2 (and_2_out, S, B);
  or or_1 (C, and_1_out, and_2_out);
endmodule

// comp
module comparador (
  input  A0,
  input  A1,
  input  A2,
  input  A3,
  input  B0,
  input  B1,
  input  B2,
  input  B3,
  output Maior,
  output Igual,
  output Menor
);

  maiorque_4_bits maiorque_4_bits_1 (
    .A0(A0), .B0(B0), .A1(A1), .B1(B1), .A2(A2), .B2(B2), .A3(A3), .B3(B3), .out_9(Maior));
  igualdade_4_bits igualdade_4_bits_1 (
    .A0(A0), .B0(B0), .A1(A1), .B1(B1), .A2(A2), .B2(B2), .A3(A3), .B3(B3), .out_9(Igual));
  maiorque_4_bits maiorque_4_bits_2 (
    .A0(B0), .B0(A0), .A1(B1), .B1(A1), .A2(B2), .B2(A2), .A3(B3), .B3(A3), .out_9(Menor));

  // Notes on the sheet:
  //   Maior
  //   Menor
endmodule

// mux
module mux2x1_4_bits (
  input  S,
  input  A0,
  input  B0,
  input  A1,
  input  B1,
  input  A2,
  input  B2,
  input  A3,
  input  B3,
  output C0,
  output C1,
  output C2,
  output C3
);

  mux mux_1 (.A(A0), .B(B0), .S(S), .C(C0));
  mux mux_2 (.A(A1), .B(B1), .S(S), .C(C1));
  mux mux_3 (.A(A2), .B(B2), .S(S), .C(C2));
  mux mux_4 (.A(A3), .B(B3), .S(S), .C(C3));
endmodule

// igual
module igualdade (
  input  A,
  input  B,
  output S
);

  wire and_1_out, and_2_out, not_1_out, not_2_out;

  not not_1 (not_1_out, A);
  and and_1 (and_1_out, not_1_out, not_2_out);
  not not_2 (not_2_out, B);
  and and_2 (and_2_out, A, B);
  or or_1 (S, and_1_out, and_2_out);
endmodule

// igual
module igualdade_4_bits (
  input  A0,
  input  B0,
  input  A1,
  input  B1,
  input  A2,
  input  B2,
  input  A3,
  input  B3,
  output out_9
);

  wire igualdade_1_s, igualdade_2_s, igualdade_3_s, igualdade_4_s;

  igualdade igualdade_1 (.A(A0), .B(B0), .S(igualdade_1_s));
  igualdade igualdade_2 (.A(A1), .B(B1), .S(igualdade_2_s));
  igualdade igualdade_3 (.A(A2), .B(B2), .S(igualdade_3_s));
  igualdade igualdade_4 (.A(A3), .B(B3), .S(igualdade_4_s));
  and and_1 (out_9, igualdade_1_s, igualdade_2_s, igualdade_3_s, igualdade_4_s);
endmodule

module maiorque_4_bits (
  input  A0,
  input  B0,
  input  A1,
  input  B1,
  input  A2,
  input  B2,
  input  A3,
  input  B3,
  output out_9
);

  wire and_1_out, and_2_out, and_3_out, igualdade_1_s, igualdade_2_s, igualdade_3_s, maiorque_1_s,
       maiorque_2_s, maiorque_3_s, maiorque_4_s;

  maiorque maiorque_1 (.A(A0), .B(B0), .S(maiorque_1_s));
  igualdade igualdade_1 (.A(A1), .B(B1), .S(igualdade_1_s));
  maiorque maiorque_2 (.A(A1), .B(B1), .S(maiorque_2_s));
  igualdade igualdade_2 (.A(A2), .B(B2), .S(igualdade_2_s));
  maiorque maiorque_3 (.A(A2), .B(B2), .S(maiorque_3_s));
  igualdade igualdade_3 (.A(A3), .B(B3), .S(igualdade_3_s));
  and and_1 (and_1_out, maiorque_1_s, igualdade_1_s, igualdade_2_s, igualdade_3_s);
  and and_2 (and_2_out, maiorque_2_s, igualdade_2_s, igualdade_3_s);
  and and_3 (and_3_out, maiorque_3_s, igualdade_3_s);
  maiorque maiorque_4 (.A(A3), .B(B3), .S(maiorque_4_s));
  or or_1 (out_9, and_1_out, and_2_out, and_3_out, maiorque_4_s);
endmodule

// maior
module maiorque (
  input  A,
  input  B,
  output S
);

  wire not_1_out;

  not not_1 (not_1_out, B);
  and and_1 (S, A, not_1_out);
endmodule

// D_A
module d_a (
  input  B3,
  input  B2,
  input  B1,
  input  B0,
  output A
);

  wire and_1_out, and_2_out, and_3_out, and_4_out, and_5_out, and_6_out;

  and and_1 (and_1_out, B3, ~B2, ~B1);  // AND_Gate
  and and_2 (and_2_out, B1, B2);
  and and_3 (and_3_out, ~B3, B1);  // AND_Gate
  and and_4 (and_4_out, ~B3, B2, B0);  // AND_Gate
  and and_5 (and_5_out, B3, ~B1, ~B0);  // AND_Gate
  and and_6 (and_6_out, ~B2, ~B0);  // AND_Gate
  or or_1 (A, and_1_out, and_2_out, and_3_out, and_4_out, and_5_out, and_6_out);
endmodule

// D_B
module d_b (
  input  B3,
  input  B2,
  input  B1,
  input  B0,
  output B
);

  wire and_1_out, and_2_out, and_3_out, and_4_out, and_5_out;

  and and_1 (and_1_out, ~B3, B1, B0);  // AND_Gate
  and and_2 (and_2_out, ~B3, ~B1, ~B0);  // AND_Gate
  and and_3 (and_3_out, B3, ~B1, B0);  // AND_Gate
  and and_4 (and_4_out, ~B3, ~B2);  // AND_Gate
  and and_5 (and_5_out, ~B2, ~B0);  // AND_Gate
  or or_1 (B, and_1_out, and_2_out, and_3_out, and_4_out, and_5_out);
endmodule

// D_C
module d_c (
  input  B3,
  input  B2,
  input  B1,
  input  B0,
  output C
);

  wire and_1_out, and_2_out, and_3_out, and_4_out, and_5_out;

  and and_1 (and_1_out, B3, ~B2);  // AND_Gate
  and and_2 (and_2_out, ~B3, B2);  // AND_Gate
  and and_3 (and_3_out, ~B1, B0);  // AND_Gate
  and and_4 (and_4_out, ~B3, ~B1);  // AND_Gate
  and and_5 (and_5_out, ~B3, B0);  // AND_Gate
  or or_1 (C, and_1_out, and_2_out, and_3_out, and_4_out, and_5_out);
endmodule

// D_D
module d_d (
  input  B3,
  input  B2,
  input  B1,
  input  B0,
  output D
);

  wire and_1_out, and_2_out, and_3_out, and_4_out, and_5_out, and_6_out;

  and and_1 (and_1_out, B2, B1, ~B0);  // AND_Gate
  and and_2 (and_2_out, ~B3, ~B2, B1);  // AND_Gate
  and and_3 (and_3_out, ~B3, ~B2, ~B0);  // AND_Gate
  and and_4 (and_4_out, B2, ~B1, B0);  // AND_Gate
  and and_5 (and_5_out, B3, ~B2, B0);  // AND_Gate
  and and_6 (and_6_out, B3, ~B1);  // AND_Gate
  or or_1 (D, and_1_out, and_2_out, and_3_out, and_4_out, and_5_out, and_6_out);
endmodule

// D_E
module d_e (
  input  B3,
  input  B2,
  input  B1,
  input  B0,
  output E
);

  wire and_1_out, and_2_out, and_3_out, and_4_out;

  and and_1 (and_1_out, B3, B2);
  and and_2 (and_2_out, B3, B1);
  and and_3 (and_3_out, ~B2, ~B1, ~B0);  // AND_Gate
  and and_4 (and_4_out, B1, ~B0);  // AND_Gate
  or or_1 (E, and_1_out, and_2_out, and_3_out, and_4_out);
endmodule

// D_F
module d_f (
  input  B3,
  input  B2,
  input  B1,
  input  B0,
  output F
);

  wire and_1_out, and_2_out, and_3_out, and_4_out, and_5_out;

  and and_1 (and_1_out, ~B3, B2, ~B1);  // AND_Gate
  and and_2 (and_2_out, B2, B1, ~B0);  // AND_Gate
  and and_3 (and_3_out, B3, B1);
  and and_4 (and_4_out, B3, ~B2);  // AND_Gate
  and and_5 (and_5_out, ~B1, ~B0);  // AND_Gate
  or or_1 (F, and_1_out, and_2_out, and_3_out, and_4_out, and_5_out);
endmodule

// D_G
module d_g (
  input  B3,
  input  B2,
  input  B1,
  input  B0,
  output G
);

  wire and_1_out, and_2_out, and_3_out, and_4_out, and_5_out;

  and and_1 (and_1_out, ~B3, ~B2, B1);  // AND_Gate
  and and_2 (and_2_out, ~B3, B2, ~B1);  // AND_Gate
  and and_3 (and_3_out, B3, ~B2);  // AND_Gate
  and and_4 (and_4_out, B3, B0);
  and and_5 (and_5_out, B1, ~B0);  // AND_Gate
  or or_1 (G, and_1_out, and_2_out, and_3_out, and_4_out, and_5_out);
endmodule

module decode (
  input  B3,
  input  B2,
  input  B1,
  input  B0,
  output D_A,
  output D_B,
  output D_C,
  output D_D,
  output D_E,
  output D_F,
  output D_G
);

  d_a d_a_1 (.B3(B3), .B2(B2), .B1(B1), .B0(B0), .A(D_A));
  d_b d_b_1 (.B3(B3), .B2(B2), .B1(B1), .B0(B0), .B(D_B));
  d_c d_c_1 (.B3(B3), .B2(B2), .B1(B1), .B0(B0), .C(D_C));
  d_d d_d_1 (.B3(B3), .B2(B2), .B1(B1), .B0(B0), .D(D_D));
  d_e d_e_1 (.B3(B3), .B2(B2), .B1(B1), .B0(B0), .E(D_E));
  d_f d_f_1 (.B3(B3), .B2(B2), .B1(B1), .B0(B0), .F(D_F));
  d_g d_g_1 (.B3(B3), .B2(B2), .B1(B1), .B0(B0), .G(D_G));
endmodule
